// Logisim project FINALS_clock.circ as structural Verilog: 10 circuits, main circuit seven-segment-two-digits
module seven_segment (
  input  A,
  input  B,
  input  C,
  input  D
);

  wire a_a1, b_b1, c_c1, d_d1, e_e1, f_f1, g_g1;

  a u_a (.A(A), .B(B), .C(C), .D(D), .a1(a_a1));  // open: a2
  b u_b (.A(A), .B(B), .C(C), .D(D), .b1(b_b1));  // open: b2
  c u_c (.A(A), .B(B), .C(C), .D(D), .c1(c_c1));  // open: c2
  d u_d (.A(A), .B(B), .C(C), .D(D), .d1(d_d1));  // open: d2
  e e (.A(A), .B(B), .C(C), .D(D), .e1(e_e1));  // open: e2
  f f (.A(A), .B(B), .C(C), .D(D), .f1(f_f1));  // open: f2
  g g (.A(A), .B(B), .C(C), .D(D), .g1(g_g1));  // open: g2
  _7_Segment_Display u_7_segment_display_1 (
    .g(g_g1), .f(f_f1), .a(a_a1), .b(b_b1), .e(e_e1), .d(d_d1), .c(c_c1));  // open: dp
endmodule

module a (
  input  A,
  input  B,
  input  C,
  input  D,
  output a1,
  output a2
);

  wire and_1_out, and_2_out, and_3_out, and_4_out, and_5_out, not_1_out, not_2_out, not_3_out, not_4_out,
       not_5_out, not_6_out, not_7_out;

  not not_1 (not_1_out, A);
  not not_2 (not_2_out, B);
  and and_1 (and_1_out, not_2_out, not_3_out);
  not not_3 (not_3_out, C);
  not not_4 (not_4_out, B);
  and and_2 (and_2_out, not_4_out, not_5_out);
  not not_5 (not_5_out, D);
  not not_6 (not_6_out, A);
  and and_3 (and_3_out, not_6_out, C);
  and and_4 (and_4_out, B, D);
  and and_5 (and_5_out, A, not_7_out);
  not not_7 (not_7_out, C);
  or or_1 (a1, not_1_out, and_1_out);
  or or_2 (a2, and_2_out, and_3_out, and_4_out, and_5_out);
  _7_Segment_Display u_7_segment_display_1 (.a(a1));  // open: g, f, b, e, d, c, dp
  _7_Segment_Display u_7_segment_display_2 (.a(a2));  // open: g, f, b, e, d, c, dp
endmodule

module b (
  input  A,
  input  B,
  input  C,
  input  D,
  output b1,
  output b2
);

  wire and_1_out, and_2_out, and_3_out, and_4_out, not_1_out, not_2_out, not_3_out, not_4_out, not_5_out,
       not_6_out;

  not not_1 (not_1_out, B);
  not not_2 (not_2_out, C);
  and and_1 (and_1_out, not_2_out, not_3_out);
  not not_3 (not_3_out, D);
  not not_4 (not_4_out, A);
  and and_2 (and_2_out, not_4_out, C, D);
  and and_3 (and_3_out, A, not_5_out);
  not not_5 (not_5_out, C);
  and and_4 (and_4_out, A, not_6_out);
  not not_6 (not_6_out, D);
  or or_1 (b2, not_1_out, and_1_out, and_2_out, and_3_out, and_4_out);

  assign b1 = 1'b1;
endmodule

module c (
  input  A,
  input  B,
  input  C,
  input  D,
  output c1,
  output c2
);

  wire and_1_out, and_2_out, and_3_out, not_1_out, not_2_out, not_3_out;

  not not_1 (not_1_out, A);
  and and_1 (and_1_out, not_1_out, not_2_out);
  not not_2 (not_2_out, C);
  and and_2 (and_2_out, B, C);
  and and_3 (and_3_out, A, not_3_out);
  not not_3 (not_3_out, B);
  or or_1 (c2, and_1_out, D, and_2_out, and_3_out);

  assign c1 = 1'b1;
endmodule

module d (
  input  A,
  input  B,
  input  C,
  input  D,
  output d1,
  output d2
);

  wire and_1_out, and_2_out, and_3_out, and_4_out, and_5_out, and_6_out, and_7_out, not_1_out, not_2_out,
       not_3_out, not_4_out, not_5_out, not_6_out, not_7_out, not_8_out, not_9_out, not_10_out, not_11_out;

  not not_1 (not_1_out, A);
  not not_2 (not_2_out, B);
  and and_1 (and_1_out, not_2_out, not_3_out);
  not not_3 (not_3_out, C);
  not not_4 (not_4_out, B);
  and and_2 (and_2_out, not_4_out, not_5_out);
  not not_5 (not_5_out, D);
  not not_6 (not_6_out, A);
  not not_7 (not_7_out, B);
  and and_3 (and_3_out, not_6_out, not_7_out, C);
  not not_8 (not_8_out, A);
  and and_4 (and_4_out, not_8_out, C, not_9_out);
  not not_9 (not_9_out, D);
  and and_5 (and_5_out, B, not_10_out, D);
  not not_10 (not_10_out, C);
  and and_6 (and_6_out, A, not_11_out);
  not not_11 (not_11_out, C);
  and and_7 (and_7_out, A, B, D);
  or or_1 (d1, not_1_out, and_1_out);
  or or_2 (d2, and_2_out, and_3_out, and_4_out, and_5_out, and_6_out, and_7_out);
endmodule

module e (
  input  A,
  input  B,
  input  C,
  input  D,
  output e1,
  output e2
);

  wire and_1_out, and_2_out, and_3_out, and_4_out, not_1_out, not_2_out, not_3_out, not_4_out, not_5_out,
       not_6_out, not_7_out, not_8_out, not_9_out;

  not not_1 (not_1_out, A);
  not not_2 (not_2_out, B);
  and and_1 (and_1_out, not_2_out, not_3_out);
  not not_3 (not_3_out, C);
  not not_4 (not_4_out, B);
  and and_2 (and_2_out, not_4_out, not_5_out);
  not not_5 (not_5_out, D);
  not not_6 (not_6_out, A);
  and and_3 (and_3_out, not_6_out, C, not_7_out);
  not not_7 (not_7_out, D);
  and and_4 (and_4_out, A, not_8_out, not_9_out);
  not not_8 (not_8_out, C);
  not not_9 (not_9_out, D);
  or or_1 (e1, not_1_out, and_1_out);
  or or_2 (e2, and_2_out, and_3_out, and_4_out);
endmodule

module f (
  input  A,
  input  B,
  input  C,
  input  D,
  output f1,
  output f2
);

  wire and_1_out, and_2_out, and_3_out, and_4_out, and_5_out, and_6_out, and_7_out, not_1_out, not_2_out,
       not_3_out, not_4_out, not_5_out, not_6_out, not_7_out, not_8_out, not_9_out, not_10_out, not_11_out,
       not_12_out, not_13_out, not_14_out;

  not not_1 (not_1_out, A);
  not not_2 (not_2_out, B);
  and and_1 (and_1_out, not_2_out, not_3_out);
  not not_3 (not_3_out, C);
  not not_4 (not_4_out, A);
  not not_5 (not_5_out, C);
  and and_2 (and_2_out, not_4_out, not_5_out, not_6_out);
  not not_6 (not_6_out, D);
  not not_7 (not_7_out, A);
  and and_3 (and_3_out, not_7_out, B, not_8_out);
  not not_8 (not_8_out, C);
  not not_9 (not_9_out, A);
  and and_4 (and_4_out, not_9_out, B, not_10_out);
  not not_10 (not_10_out, D);
  not not_11 (not_11_out, B);
  and and_5 (and_5_out, A, not_11_out, not_12_out);
  not not_12 (not_12_out, C);
  and and_6 (and_6_out, A, not_13_out, not_14_out);
  not not_13 (not_13_out, B);
  not not_14 (not_14_out, D);
  and and_7 (and_7_out, A, B, C);
  or or_1 (f1, not_1_out, and_1_out);
  or or_2 (f2, and_2_out, and_3_out, and_4_out, and_5_out, and_6_out, and_7_out);
endmodule

module g (
  input  A,
  input  B,
  input  C,
  input  D,
  output g1,
  output g2
);

  wire and_1_out, and_2_out, and_3_out, and_4_out, and_5_out, not_1_out, not_2_out, not_3_out, not_4_out,
       not_5_out;

  not not_1 (not_1_out, A);
  and and_1 (and_1_out, not_1_out, not_2_out, C);
  not not_2 (not_2_out, B);
  and and_2 (and_2_out, B, not_3_out);
  not not_3 (not_3_out, C);
  and and_3 (and_3_out, B, not_4_out);
  not not_4 (not_4_out, D);
  and and_4 (and_4_out, A, not_5_out);
  not not_5 (not_5_out, C);
  and and_5 (and_5_out, A, B);
  or or_1 (g2, and_1_out, and_2_out, and_3_out, and_4_out, and_5_out);

  assign g1 = 1'b0;
endmodule

module seven_segment_two_digits (
  input  TOMBOL_HIDUP,
  output D,
  output C,
  output B,
  output A,
  output D_2,
  output C_2,
  output B_2,
  output A_2,
  output D_3,
  output C_3,
  output B_3,
  output A_3
);

  wire a_2_a1, a_2_a2, a_3_a1, a_3_a2, a_a1, a_a2, and_1_out, and_2_out, and_3_out, b_2_b1, b_2_b2, b_3_b1,
       b_3_b2, b_b1, b_b2, c_2_c1, c_2_c2, c_3_c1, c_3_c2, c_c1, c_c2, clock_1_out, d_2_d1, d_2_d2, d_3_d1,
       d_3_d2, d_d1, d_d2, e_2_e1, e_2_e2, e_3_e1, e_3_e2, e_e1, e_e2, f_2_f1, f_2_f2, f_3_f1, f_3_f2, f_f1,
       f_f2, g_2_g1, g_2_g2, g_3_g1, g_3_g2, g_g1, g_g2, j_k_ff_1_q, j_k_ff_2_q, j_k_ff_3_q, j_k_ff_5_q,
       j_k_ff_6_q, j_k_ff_7_q, j_k_ff_8_q, j_k_ff_9_q, j_k_ff_10_q, PAUSE_out, RESET_out, transistor_1_out,
       transistor_2_out, transistor_3_out, transistor_4_out;

  J_K_Flip_Flop j_k_ff_1 (
    .J(transistor_4_out), .clk(and_2_out), .K(transistor_4_out), .Q(j_k_ff_1_q), .Qn(D_2),
    .preset(and_1_out), .en(transistor_4_out), .reset(RESET_out));
  J_K_Flip_Flop j_k_ff_2 (
    .J(transistor_4_out), .clk(j_k_ff_1_q), .K(transistor_4_out), .Q(j_k_ff_2_q), .Qn(C_2),
    .preset(and_1_out), .en(transistor_4_out), .reset(RESET_out));
  J_K_Flip_Flop j_k_ff_3 (
    .J(transistor_4_out), .clk(j_k_ff_2_q), .K(transistor_4_out), .Q(j_k_ff_3_q), .Qn(B_2),
    .preset(and_1_out), .en(transistor_4_out), .reset(RESET_out));
  J_K_Flip_Flop j_k_ff_4 (
    .J(transistor_4_out), .clk(j_k_ff_3_q), .K(transistor_4_out), .Qn(A_2), .preset(and_1_out),
    .reset(RESET_out));  // open: Q, en
  and and_1 (and_1_out, D_2, C_2, B_2, A_2);
  a u_a (.A(A_2), .B(B_2), .C(C_2), .D(D_2), .a1(a_a1), .a2(a_a2));
  b u_b (.A(A_2), .B(B_2), .C(C_2), .D(D_2), .b1(b_b1), .b2(b_b2));
  c u_c (.A(A_2), .B(B_2), .C(C_2), .D(D_2), .c1(c_c1), .c2(c_c2));
  d u_d (.A(A_2), .B(B_2), .C(C_2), .D(D_2), .d1(d_d1), .d2(d_d2));
  e e (.A(A_2), .B(B_2), .C(C_2), .D(D_2), .e1(e_e1), .e2(e_e2));
  f f (.A(A_2), .B(B_2), .C(C_2), .D(D_2), .f1(f_f1), .f2(f_f2));
  g g (.A(A_2), .B(B_2), .C(C_2), .D(D_2), .g1(g_g1), .g2(g_g2));
  a u_a_2 (.A(A), .B(B), .C(C), .D(D), .a1(a_2_a1), .a2(a_2_a2));
  c u_c_2 (.A(A), .B(B), .C(C), .D(D), .c1(c_2_c1), .c2(c_2_c2));
  b u_b_2 (.A(A), .B(B), .C(C), .D(D), .b1(b_2_b1), .b2(b_2_b2));
  _7_Segment_Display u_7_segment_display_1 (
    .g(g_g1), .f(f_f1), .a(a_a1), .b(b_b1), .e(e_e1), .d(d_d1), .c(c_c1));  // open: dp
  d u_d_2 (.A(A), .B(B), .C(C), .D(D), .d1(d_2_d1), .d2(d_2_d2));
  _7_Segment_Display u_7_segment_display_2 (
    .g(g_g2), .f(f_f2), .a(a_a2), .b(b_b2), .e(e_e2), .d(d_d2), .c(c_c2));  // open: dp
  a u_a_3 (.A(A_3), .B(B_3), .C(C_3), .D(D_3), .a1(a_3_a1), .a2(a_3_a2));
  b u_b_3 (.A(A_3), .B(B_3), .C(C_3), .D(D_3), .b1(b_3_b1), .b2(b_3_b2));
  f f_2 (.A(A), .B(B), .C(C), .D(D), .f1(f_2_f1), .f2(f_2_f2));
  e e_2 (.A(A), .B(B), .C(C), .D(D), .e1(e_2_e1), .e2(e_2_e2));
  c u_c_3 (.A(A_3), .B(B_3), .C(C_3), .D(D_3), .c1(c_3_c1), .c2(c_3_c2));
  g g_2 (.A(A), .B(B), .C(C), .D(D), .g1(g_2_g1), .g2(g_2_g2));
  _7_Segment_Display u_7_segment_display_3 (
    .g(g_2_g1), .f(f_2_f1), .a(a_2_a1), .b(b_2_b1), .e(e_2_e1), .d(d_2_d1), .c(c_2_c1));  // open: dp
  d u_d_3 (.A(A_3), .B(B_3), .C(C_3), .D(D_3), .d1(d_3_d1), .d2(d_3_d2));
  e e_3 (.A(A_3), .B(B_3), .C(C_3), .D(D_3), .e1(e_3_e1), .e2(e_3_e2));
  Clock clock_1 (.out(clock_1_out));
  Transistor #(.\type ("n")) transistor_1 (.in(and_3_out), .out(transistor_1_out), .gate(transistor_4_out));
  _7_Segment_Display u_7_segment_display_4 (
    .g(g_2_g2), .f(f_2_f2), .a(a_2_a2), .b(b_2_b2), .e(e_2_e2), .d(d_2_d2), .c(c_2_c2));  // open: dp
  f f_3 (.A(A_3), .B(B_3), .C(C_3), .D(D_3), .f1(f_3_f1), .f2(f_3_f2));
  g g_3 (.A(A_3), .B(B_3), .C(C_3), .D(D_3), .g1(g_3_g1), .g2(g_3_g2));
  Transistor #(.\type ("n")) transistor_2 (.in(clock_1_out), .out(transistor_2_out), .gate(transistor_4_out));
  J_K_Flip_Flop j_k_ff_5 (
    .J(transistor_4_out), .clk(transistor_1_out), .K(transistor_4_out), .Q(j_k_ff_5_q), .Qn(D),
    .preset(and_2_out), .en(transistor_4_out), .reset(RESET_out));
  _7_Segment_Display u_7_segment_display_5 (
    .g(g_3_g1), .f(f_3_f1), .a(a_3_a1), .b(b_3_b1), .e(e_3_e1), .d(d_3_d1), .c(c_3_c1));  // open: dp
  J_K_Flip_Flop j_k_ff_6 (
    .J(transistor_4_out), .clk(transistor_2_out), .K(transistor_4_out), .Q(j_k_ff_6_q), .Qn(D_3),
    .preset(and_3_out), .en(transistor_4_out), .reset(RESET_out));
  J_K_Flip_Flop j_k_ff_7 (
    .J(transistor_4_out), .clk(j_k_ff_5_q), .K(transistor_4_out), .Q(j_k_ff_7_q), .Qn(C), .preset(and_2_out),
    .en(transistor_4_out), .reset(RESET_out));
  Button PAUSE (.out(PAUSE_out));
  _7_Segment_Display u_7_segment_display_6 (
    .g(g_3_g2), .f(f_3_f2), .a(a_3_a2), .b(b_3_b2), .e(e_3_e2), .d(d_3_d2), .c(c_3_c2));  // open: dp
  J_K_Flip_Flop j_k_ff_8 (
    .J(transistor_4_out), .clk(j_k_ff_6_q), .K(transistor_4_out), .Q(j_k_ff_8_q), .Qn(C_3),
    .preset(and_3_out), .en(transistor_4_out), .reset(RESET_out));
  J_K_Flip_Flop j_k_ff_9 (
    .J(transistor_4_out), .clk(j_k_ff_7_q), .K(transistor_4_out), .Q(j_k_ff_9_q), .Qn(B), .preset(and_2_out),
    .en(transistor_4_out), .reset(RESET_out));
  Button RESET (.out(RESET_out));
  Transistor #(.\type ("n")) transistor_3 (.in(TOMBOL_HIDUP), .out(transistor_3_out), .gate(TOMBOL_HIDUP));
  Transistor transistor_4 (.in(transistor_3_out), .out(transistor_4_out), .gate(PAUSE_out));
  J_K_Flip_Flop j_k_ff_10 (
    .J(transistor_4_out), .clk(j_k_ff_8_q), .K(transistor_4_out), .Q(j_k_ff_10_q), .Qn(B_3),
    .preset(and_3_out), .en(transistor_4_out), .reset(RESET_out));
  J_K_Flip_Flop j_k_ff_11 (
    .J(transistor_4_out), .clk(j_k_ff_9_q), .K(transistor_4_out), .Qn(A), .preset(and_2_out),
    .en(transistor_4_out), .reset(RESET_out));  // open: Q
  J_K_Flip_Flop j_k_ff_12 (
    .J(transistor_4_out), .clk(j_k_ff_10_q), .K(transistor_4_out), .Qn(A_3), .preset(and_3_out),
    .en(transistor_4_out), .reset(RESET_out));  // open: Q
  and and_2 (and_2_out, A, B, C, D);
  and and_3 (and_3_out, B_3, D_3, A_3);

  // Notes on the sheet:
  //   JAM
  //   DETIK
  //   MENIT
  //   HIDUPKAN "TICK ENABLED" di settings
endmodule

module jk_flip_flop (
  input  in_1,
  output out_2,
  output out_3,
  output out_4,
  output out_5,
  output out_6,
  output out_7,
  output out_8,
  output out_9,
  output out_10,
  output out_11,
  output out_12,
  output out_13
);

  wire a_1_a1, a_1_a2, a_2_a1, a_2_a2, a_3_a1, a_3_a2, and_1_out, and_2_out, and_3_out, b_2_b1, b_2_b2,
       b_3_b1, b_3_b2, b_b1, b_b2, button_1_out, c_2_c1, c_2_c2, c_3_c1, c_3_c2, c_c1, c_c2, clock_1_out,
       d_2_d1, d_2_d2, d_3_d1, d_3_d2, d_d1, d_d2, e_2_e1, e_2_e2, e_3_e1, e_3_e2, e_e1, e_e2, f_2_f1,
       f_2_f2, f_3_f1, f_3_f2, f_f1, f_f2, g_1_g1, g_1_g2, g_2_g1, g_2_g2, g_3_g1, g_3_g2, j_k_ff_1_q,
       j_k_ff_2_q, j_k_ff_3_q, j_k_ff_5_q, j_k_ff_6_q, j_k_ff_7_q, j_k_ff_9_q, j_k_ff_10_q, j_k_ff_11_q,
       RESET_out, transistor_1_out;

  Clock clock_1 (.out(clock_1_out));
  Button button_1 (.out(button_1_out));
  Transistor transistor_1 (.in(in_1), .out(transistor_1_out), .gate(button_1_out));
  a a_1 (.A(out_2), .B(out_3), .C(out_4), .D(out_5), .a1(a_1_a1), .a2(a_1_a2));
  b b (.A(out_2), .B(out_3), .C(out_4), .D(out_5), .b1(b_b1), .b2(b_b2));
  c c (.A(out_2), .B(out_3), .C(out_4), .D(out_5), .c1(c_c1), .c2(c_c2));
  d d (.A(out_2), .B(out_3), .C(out_4), .D(out_5), .d1(d_d1), .d2(d_d2));
  e e (.A(out_2), .B(out_3), .C(out_4), .D(out_5), .e1(e_e1), .e2(e_e2));
  f f (.A(out_2), .B(out_3), .C(out_4), .D(out_5), .f1(f_f1), .f2(f_f2));
  g g_1 (.A(out_2), .B(out_3), .C(out_4), .D(out_5), .g1(g_1_g1), .g2(g_1_g2));
  J_K_Flip_Flop j_k_ff_1 (
    .J(transistor_1_out), .clk(clock_1_out), .K(transistor_1_out), .Q(j_k_ff_1_q), .Qn(out_5),
    .preset(and_1_out), .en(transistor_1_out), .reset(RESET_out));
  Button RESET (.out(RESET_out));
  _7_Segment_Display u_7_segment_display_1 (
    .g(g_1_g1), .f(f_f1), .a(a_1_a1), .b(b_b1), .e(e_e1), .d(d_d1), .c(c_c1));  // open: dp
  J_K_Flip_Flop j_k_ff_2 (
    .J(transistor_1_out), .clk(j_k_ff_1_q), .K(transistor_1_out), .Q(j_k_ff_2_q), .Qn(out_4),
    .preset(and_1_out), .en(transistor_1_out), .reset(RESET_out));
  _7_Segment_Display u_7_segment_display_2 (
    .g(g_1_g2), .f(f_f2), .a(a_1_a2), .b(b_b2), .e(e_e2), .d(d_d2), .c(c_c2));  // open: dp
  J_K_Flip_Flop j_k_ff_3 (
    .J(transistor_1_out), .clk(j_k_ff_2_q), .K(transistor_1_out), .Q(j_k_ff_3_q), .Qn(out_3),
    .preset(and_1_out), .en(transistor_1_out), .reset(RESET_out));
  J_K_Flip_Flop j_k_ff_4 (
    .J(transistor_1_out), .clk(j_k_ff_3_q), .K(transistor_1_out), .Qn(out_2), .preset(and_1_out),
    .en(transistor_1_out), .reset(RESET_out));  // open: Q
  and and_1 (and_1_out, out_2, out_4, out_5);
  a a_2 (.A(out_6), .B(out_7), .C(out_8), .D(out_9), .a1(a_2_a1), .a2(a_2_a2));
  b b_2 (.A(out_6), .B(out_7), .C(out_8), .D(out_9), .b1(b_2_b1), .b2(b_2_b2));
  c c_2 (.A(out_6), .B(out_7), .C(out_8), .D(out_9), .c1(c_2_c1), .c2(c_2_c2));
  d d_2 (.A(out_6), .B(out_7), .C(out_8), .D(out_9), .d1(d_2_d1), .d2(d_2_d2));
  e e_2 (.A(out_6), .B(out_7), .C(out_8), .D(out_9), .e1(e_2_e1), .e2(e_2_e2));
  f f_2 (.A(out_6), .B(out_7), .C(out_8), .D(out_9), .f1(f_2_f1), .f2(f_2_f2));
  g g_2 (.A(out_6), .B(out_7), .C(out_8), .D(out_9), .g1(g_2_g1), .g2(g_2_g2));
  J_K_Flip_Flop j_k_ff_5 (
    .J(transistor_1_out), .clk(and_1_out), .K(transistor_1_out), .Q(j_k_ff_5_q), .Qn(out_9),
    .preset(and_2_out), .en(transistor_1_out), .reset(RESET_out));
  J_K_Flip_Flop j_k_ff_6 (
    .J(transistor_1_out), .clk(j_k_ff_5_q), .K(transistor_1_out), .Q(j_k_ff_6_q), .Qn(out_8),
    .preset(and_2_out), .en(transistor_1_out), .reset(RESET_out));
  _7_Segment_Display u_7_segment_display_3 (
    .g(g_2_g1), .f(f_2_f1), .a(a_2_a1), .b(b_2_b1), .e(e_2_e1), .d(d_2_d1), .c(c_2_c1));  // open: dp
  _7_Segment_Display u_7_segment_display_4 (
    .g(g_2_g2), .f(f_2_f2), .a(a_2_a2), .b(b_2_b2), .e(e_2_e2), .d(d_2_d2), .c(c_2_c2));  // open: dp
  J_K_Flip_Flop j_k_ff_7 (
    .J(transistor_1_out), .clk(j_k_ff_6_q), .K(transistor_1_out), .Q(j_k_ff_7_q), .Qn(out_7),
    .preset(and_2_out), .en(transistor_1_out), .reset(RESET_out));
  J_K_Flip_Flop j_k_ff_8 (
    .J(transistor_1_out), .clk(j_k_ff_7_q), .K(transistor_1_out), .Qn(out_6), .preset(and_2_out),
    .en(transistor_1_out), .reset(RESET_out));  // open: Q
  and and_2 (and_2_out, out_6, out_8, out_9);
  J_K_Flip_Flop j_k_ff_9 (
    .J(transistor_1_out), .clk(and_2_out), .K(transistor_1_out), .Q(j_k_ff_9_q), .Qn(out_13),
    .preset(and_3_out), .en(transistor_1_out), .reset(RESET_out));
  a a_3 (.A(out_10), .B(out_11), .C(out_12), .D(out_13), .a1(a_3_a1), .a2(a_3_a2));
  b b_3 (.A(out_10), .B(out_11), .C(out_12), .D(out_13), .b1(b_3_b1), .b2(b_3_b2));
  c c_3 (.A(out_10), .B(out_11), .C(out_12), .D(out_13), .c1(c_3_c1), .c2(c_3_c2));
  d d_3 (.A(out_10), .B(out_11), .C(out_12), .D(out_13), .d1(d_3_d1), .d2(d_3_d2));
  e e_3 (.A(out_10), .B(out_11), .C(out_12), .D(out_13), .e1(e_3_e1), .e2(e_3_e2));
  f f_3 (.A(out_10), .B(out_11), .C(out_12), .D(out_13), .f1(f_3_f1), .f2(f_3_f2));
  g g_3 (.A(out_10), .B(out_11), .C(out_12), .D(out_13), .g1(g_3_g1), .g2(g_3_g2));
  J_K_Flip_Flop j_k_ff_10 (
    .J(transistor_1_out), .clk(j_k_ff_9_q), .K(transistor_1_out), .Q(j_k_ff_10_q), .Qn(out_12),
    .preset(and_3_out), .en(transistor_1_out), .reset(RESET_out));
  _7_Segment_Display u_7_segment_display_5 (
    .g(g_3_g2), .f(f_3_f2), .a(a_3_a2), .b(b_3_b2), .e(e_3_e2), .d(d_3_d2), .c(c_3_c2));  // open: dp
  _7_Segment_Display u_7_segment_display_6 (
    .g(g_3_g1), .f(f_3_f1), .a(a_3_a1), .b(b_3_b1), .e(e_3_e1), .d(d_3_d1), .c(c_3_c1));  // open: dp
  J_K_Flip_Flop j_k_ff_11 (
    .J(transistor_1_out), .clk(j_k_ff_10_q), .K(transistor_1_out), .Q(j_k_ff_11_q), .Qn(out_11),
    .preset(and_3_out), .en(transistor_1_out), .reset(RESET_out));
  J_K_Flip_Flop j_k_ff_12 (
    .J(transistor_1_out), .clk(j_k_ff_11_q), .K(transistor_1_out), .Qn(out_10), .preset(and_3_out),
    .en(transistor_1_out), .reset(RESET_out));  // open: Q
  and and_3 (and_3_out, out_10, out_11, out_12);
endmodule
